# Fritzing sketch USB-Timer 3 (saved by Fritzing 0.9.6b)

parts:
  WeMos_D1_Mini1 = WeMos D1 Mini
  Q1 = MOSFET-NCHANNEL [package=to220v]
  R1 = Resistor [tolerance=±5% power=0.25 resistance=220 package=THT]
  X2 = USB Connectors [package=usb-a-s-silk-female]
  JP1 = USB_MICROB_PLUG [package=micro-b-th]
  X3 = USB Connectors [package=usb-a-s-silk-female]  # not connected
  X4 = USB Connectors [package=usb-a-s-silk-female]  # not connected
  X5 = USB Connectors [package=usb-a-s-silk-female]  # not connected
  JP2 = USB_MICROB_PLUG [package=micro-b-th]  # not connected
  JP3 = USB_MICROB_PLUG [package=micro-b-th]  # not connected
  JP4 = USB_MICROB_PLUG [package=micro-b-th]  # not connected
  Q2 = MOSFET-NCHANNEL [package=to220v]
  Q3 = MOSFET-NCHANNEL [package=to220v]
  Q4 = MOSFET-NCHANNEL [package=to220v]
  S1 = SWITCH-MOMENTARY-2 [package=tactile-pth-12mm]
  R3 = Resistor [tolerance=±5% power=0.25 resistance=220 package=THT]
  R4 = Resistor [tolerance=±5% power=0.25 resistance=220 package=THT]
  R2 = Resistor [tolerance=±5% power=0.25 resistance=220 package=THT]
  LED1 = LED - 5mm [color="Blue (525nm)" current=0.030 package="5 mm [THT]"]
  S2 = Pushbutton [package="[THT]"]
  S3 = Pushbutton [package="[THT]"]
  S4 = Pushbutton [package="[THT]"]
  S5 = Pushbutton [package="[THT]"]

nets:
  N1: WeMos_D1_Mini1.D0, S2.Pin_3, S2.Pin_4
  N2: WeMos_D1_Mini1.D1, S4.Pin_4
  N3: WeMos_D1_Mini1.D2, S5.Pin_4
  N4: WeMos_D1_Mini1.D3, S3.Pin_4
  N5: WeMos_D1_Mini1.D4, S1.1, LED1.anode
  N6: WeMos_D1_Mini1.D5, Q4.G, R4.Pin_0
  N7: WeMos_D1_Mini1.D6, Q3.G, R3.Pin_0
  N8: WeMos_D1_Mini1.D7, Q2.G, R2.Pin_0
  N9: WeMos_D1_Mini1.D8, Q1.G, R1.Pin_0
  GND: WeMos_D1_Mini1.G, Q1.S, R1.Pin_1, JP1.GND, S1.2, LED1.cathode, S2.Pin_1, S2.Pin_2, S3.Pin_1, S3.Pin_2, S4.Pin_1, S4.Pin_2, S5.Pin_2
  N10: Q1.D, X2.GND
  N11: X2.D+, JP1.D+
  N12: X2.D-, JP1.D-
  N13: X2.VBUS, JP1.VCC
  N14: Q2.S, R2.Pin_1
  N15: Q3.S, R3.Pin_1
  N16: Q4.S, R4.Pin_1

notes:
  Device 1
  D8
  Device 2
  D7
  Device 3
  D6
  Device 4
  D5
  D4 can either be wifi reset, or builtin status LED
  Computer1
  Computer2
  Computer3
  Computer4
  USB1
  D0
  USB2
  D1
  USB3
  D2
  USB4
  D3
